// Logisim project miniCPU.circ as structural Verilog: 8 circuits, main circuit testbench
module TOP (
  input  clk,
  input  rst,
  input  [31:0] inst,
  input  [31:0] memReadData,
  output [31:0] PC,
  output memWriteEnable,
  output [31:0] memWriteData,
  output [31:0] memAddress,
  output regWriteEnable,
  output [4:0] regWriteAddress,
  output [31:0] regWriteData,
  output memByteEnable3,
  output memByteEnable2,
  output memByteEnable1,
  output memByteEnable0
);

  wire AluSrcA, AluSrcB, Branch, branchTaken, condBranch, Jump, Less, MemWrite, PcAddSrcA, PCSrc, RegWrite,
       Zero;
  wire [1:0] addrLow2, ResultSrc;
  wire [2:0] BranchOp, ImmSrc, MemOp;
  wire [3:0] AluOp, lsuByteEnable;
  wire [31:0] aluSrcA_t, aluSrcB_t, ImmExt, loadResult, memWriteData_t, PC_t, pcAddSrcA_t, PCNext, pcPlus4,
       pcTarget, pcTargetRaw, RD1, RD2, regWriteData_t;
  wire [31:2] aluResult;

  Register #(.width(32)) PCReg (.D(PCNext), .en(1'b1), .clk(clk), .Q(PC_t), .clr(rst));
  Adder #(.width(32)) adder_1 (.a(PC_t), .b(32'h4), .out(pcPlus4));  // open: cin, cout
  and and_1 (condBranch, Branch, branchTaken);
  Multiplexer #(.width(32)) multiplexer_1 (.in0(pcPlus4), .in1(pcTarget), .out(PCNext), .sel(PCSrc));
  // Probe on addrLow2
  RegFile regfile_1 (
    .RA1(inst[19:15]), .RA2(inst[24:20]), .WA(inst[11:7]), .WD(regWriteData_t), .RegWrite(RegWrite),
    .clk(clk), .rst(rst), .RD1(RD1), .RD2(RD2));
  // Probe on nothing
  LSU lsu_1 (
    .Rs2(RD2), .Addr2(addrLow2), .MemOp(MemOp), .MemWrite(MemWrite), .MemReadData(memReadData),
    .MemWriteData(memWriteData_t), .MemByteEnable(lsuByteEnable), .LoadResult(loadResult));
  Multiplexer #(.select(2), .width(32)) multiplexer_2 (
    .in0({aluResult, addrLow2}), .in1(loadResult), .in2(pcPlus4), .out(regWriteData_t), .sel(ResultSrc));  // open: in3
  Control control_1 (
    .Inst(inst), .RegWrite(RegWrite), .ResultSrc(ResultSrc), .MemWrite(MemWrite), .MemOp(MemOp),
    .AluOp(AluOp), .AluSrcA(AluSrcA), .AluSrcB(AluSrcB), .PcAddSrcA(PcAddSrcA), .Branch(Branch), .Jump(Jump),
    .BranchOp(BranchOp), .ImmSrc(ImmSrc));
  BranchUnit branchunit_1 (.BranchOp(BranchOp), .Zero(Zero), .Less(Less), .Branch(branchTaken));
  Multiplexer #(.width(32)) multiplexer_3 (.in0(PC_t), .in1({32{1'b0}}), .out(PC), .sel(rst));
  Multiplexer multiplexer_4 (.in0(MemWrite), .in1(1'b0), .out(memWriteEnable), .sel(rst));
  Multiplexer #(.width(32)) multiplexer_5 (.in0(memWriteData_t), .in1({32{1'b0}}), .out(memWriteData), .sel(rst));
  Multiplexer #(.width(32)) multiplexer_6 (.in0({aluResult, addrLow2}), .in1({32{1'b0}}), .out(memAddress), .sel(rst));
  Multiplexer multiplexer_7 (.in0(RegWrite), .in1(1'b0), .out(regWriteEnable), .sel(rst));
  Multiplexer #(.width(5)) multiplexer_8 (.in0(inst[11:7]), .in1({5{1'b0}}), .out(regWriteAddress), .sel(rst));
  Multiplexer #(.width(32)) multiplexer_9 (.in0(regWriteData_t), .in1({32{1'b0}}), .out(regWriteData), .sel(rst));
  Multiplexer multiplexer_10 (.in0(lsuByteEnable[3]), .in1(1'b0), .out(memByteEnable3), .sel(rst));
  Multiplexer multiplexer_11 (.in0(lsuByteEnable[2]), .in1(1'b0), .out(memByteEnable2), .sel(rst));
  Multiplexer multiplexer_12 (.in0(lsuByteEnable[1]), .in1(1'b0), .out(memByteEnable1), .sel(rst));
  Multiplexer multiplexer_13 (.in0(lsuByteEnable[0]), .in1(1'b0), .out(memByteEnable0), .sel(rst));
  // Probe on nothing
  ImmGen immgen_1 (.Inst(inst), .ImmSrc(ImmSrc), .ImmExt(ImmExt));
  or or_1 (PCSrc, condBranch, Jump);
  Multiplexer #(.width(32)) multiplexer_14 (.in0(PC_t), .in1(RD1), .out(pcAddSrcA_t), .sel(PcAddSrcA));
  Adder #(.width(32)) adder_2 (.a(pcAddSrcA_t), .b(ImmExt), .out(pcTargetRaw));  // open: cin, cout
  assign pcTarget = pcTargetRaw & 32'hfffffffe;  // AND_Gate and_2, 32 bits wide
  Multiplexer #(.width(32)) multiplexer_15 (.in0(RD1), .in1(PC_t), .out(aluSrcA_t), .sel(AluSrcA));
  Multiplexer #(.width(32)) multiplexer_16 (.in0(RD2), .in1(ImmExt), .out(aluSrcB_t), .sel(AluSrcB));
  // Probe on AluOp
  ALU alu_1 (
    .SrcA(aluSrcA_t), .SrcB(aluSrcB_t), .AluOp(AluOp), .Result({aluResult, addrLow2}), .Zero(Zero),
    .Less(Less));

  // Other names for the same wires on the sheet: rd[4:0] = inst[11:7]; regWriteAddress_t[4:0] = inst[11:7];
  //   RA1[4:0] = inst[19:15]; RA2[4:0] = inst[24:20]; memByteEnable0_t = lsuByteEnable[0];
  //   memByteEnable1_t = lsuByteEnable[1]; memByteEnable2_t = lsuByteEnable[2]; memByteEnable3_t = lsuByteEnable[3];
  //   aluResult[1:0] = addrLow2; memAddress_t[31:0] = {aluResult, addrLow2}; memWriteEnable_t = MemWrite;
  //   regWriteEnable_t = RegWrite; wbData[31:0] = regWriteData_t

  // Notes on the sheet:
  //   DON'T TOUCH!
endmodule

module testbench (
  input  rst,
  output [5:0] count,
  output [31:0] memReadData,
  output halt,
  output [31:0] memAddress,
  output memWriteEnable,
  output [31:0] memWriteData,
  output memByteEnable3,
  output memByteEnable2,
  output memByteEnable1,
  output memByteEnable0,
  output regWriteEnable,
  output [4:0] regWriteAddress,
  output [31:0] regWriteData
);

  wire and_1_out, carry, clk, not_1_out, not_2_out, por_1_out, rst_t;
  wire [31:0] inst, PC;

  not not_1 (not_1_out, inst[2]);
  not not_2 (not_2_out, inst[3]);
  POR por_1 (.out(por_1_out));
  TOP top_1 (
    .clk(clk), .rst(rst_t), .inst(inst), .memReadData(memReadData), .PC(PC), .memWriteEnable(memWriteEnable),
    .memWriteData(memWriteData), .memAddress(memAddress), .regWriteEnable(regWriteEnable),
    .regWriteAddress(regWriteAddress), .regWriteData(regWriteData), .memByteEnable3(memByteEnable3),
    .memByteEnable2(memByteEnable2), .memByteEnable1(memByteEnable1), .memByteEnable0(memByteEnable0));
  Clock clock_1 (.out(clk));
  or or_1 (rst_t, rst, por_1_out);
  and and_1 (and_1_out, inst[0], inst[1], not_1_out, not_2_out, inst[4], inst[5], inst[6]);
  or or_2 (halt, and_1_out, carry);
  Counter #(.max('h3f), .width(6)) counter_1 (
    .clr(rst_t), .up(1'b1), .count(1'b1), .clk(clk), .carry(carry), .Q(count));  // open: load, D
  // Probe on PC
  // Probe on PC[9:2]
  ROM #(.dataWidth(32), .misaligned("true")) rom_1 (.addr(PC[9:2]), .data(inst));
  // Probe on inst
  RAM #(.asyncread("true"), .byteenables("byteEnables"), .dataWidth(32)) ram_1 (
    .addr(memAddress[9:2]), .we(memWriteEnable), .clk(clk), .din(memWriteData), .dout(memReadData),
    .be3(memByteEnable3), .be2(memByteEnable2), .be1(memByteEnable1), .be0(memByteEnable0));  // open: oe

  // Notes on the sheet:
  //   DON'T TOUCH!
  //   contents of rom_1 (hex, n*v repeats v):
  //   20000db7 3300913 500993 100493 700a13 ff900a93 ccccfb37 effb0b13 297 5da023 4d8d93 14282e7 293
  //   5da023 4d8d93 8002ef 293 5da023 4d8d93 16da023 d8d13 4d8d93 d81a3 d8123 d8023 16d80a3 4d8d93 d2283
  //   5da023 4d8d93 d0283 5da023 4d8d93 13902b3 5da023 4d8d93 413902b3 5da023 4d8d93 13972b3 5da023 4d8d93
  //   144a2b3 5da023 4d8d93 ff690293 5da023 4d8d93 39f293 5da023 4d8d93 4a293 5da023 4d8d93 100293 14a8463
  //   293 5da023 4d8d93 100293 14ac463 293 5da023 4d8d93 100073
  //   you can write any instruction in
  //   D_MEM
endmodule

module ALU (
  input  [31:0] SrcA,
  input  [31:0] SrcB,
  input  [3:0] AluOp,
  output [31:0] Result,
  output Zero,
  output Less
);

  wire [31:0] adder_1_out, and_1_out, bit_extender_1_out, or_1_out, subtractor_1_out;

  Adder #(.width(32)) adder_1 (.a(SrcA), .b(SrcB), .out(adder_1_out));  // open: cin, cout
  Subtractor #(.width(32)) subtractor_1 (.a(SrcA), .b(SrcB), .out(subtractor_1_out));  // open: bin, bout
  Comparator #(.width(32)) comparator_1 (.a(SrcA), .b(SrcB), .lt(Less));  // open: gt, eq
  assign or_1_out = SrcA | SrcB;  // OR_Gate or_1, 32 bits wide
  assign and_1_out = SrcA & SrcB;  // AND_Gate and_1, 32 bits wide
  assign bit_extender_1_out = {{31{1'b0}}, Less};  // Bit_Extender bit_extender_1
  Multiplexer #(.select(4), .width(32)) multiplexer_1 (
    .in0(adder_1_out), .in1(subtractor_1_out), .in2(and_1_out), .in5(bit_extender_1_out), .in6(or_1_out),
    .in10(SrcB), .out(Result), .sel(AluOp));  // open: in3, in4, in7, in8, in9, in11, in12, in13, in14, in15
  Comparator #(.width(32)) comparator_2 (.a(Result), .b({32{1'b0}}), .eq(Zero));  // open: gt, lt
endmodule

module RegFile (
  input  [4:0] RA1,
  input  [4:0] RA2,
  input  [4:0] WA,
  input  [31:0] WD,
  input  RegWrite,
  input  clk,
  input  rst,
  output [31:0] RD1,
  output [31:0] RD2
);

  wire WE1, WE2, WE3, WE4, WE5, WE6, WE7, WE8, WE9, WE10, WE11, WE12, WE13, WE14, WE15, WE16, WE17, WE18,
       WE19, WE20, WE21, WE22, WE23, WE24, WE25, WE26, WE27, WE28, WE29, WE30, WE31;
  wire [31:0] Q1, Q2, Q3, Q4, Q5, Q6, Q7, Q8, Q9, Q10, Q11, Q12, Q13, Q14, Q15, Q16, Q17, Q18, Q19, Q20, Q21,
       Q22, Q23, Q24, Q25, Q26, Q27, Q28, Q29, Q30, Q31;

  Decoder #(.select(5)) decoder_1 (
    .out1(WE1), .out2(WE2), .out3(WE3), .out4(WE4), .out5(WE5), .out6(WE6), .out7(WE7), .out8(WE8),
    .out9(WE9), .out10(WE10), .out11(WE11), .out12(WE12), .out13(WE13), .out14(WE14), .out15(WE15),
    .out16(WE16), .out17(WE17), .out18(WE18), .out19(WE19), .out20(WE20), .out21(WE21), .out22(WE22),
    .out23(WE23), .out24(WE24), .out25(WE25), .out26(WE26), .out27(WE27), .out28(WE28), .out29(WE29),
    .out30(WE30), .out31(WE31), .sel(WA), .en(RegWrite));  // open: out0
  Register #(.width(32)) x1 (.D(WD), .en(WE1), .clk(clk), .Q(Q1), .clr(rst));
  Register #(.width(32)) X2 (.D(WD), .en(WE2), .clk(clk), .Q(Q2), .clr(rst));
  Register #(.width(32)) x3 (.D(WD), .en(WE3), .clk(clk), .Q(Q3), .clr(rst));
  Register #(.width(32)) x4 (.D(WD), .en(WE4), .clk(clk), .Q(Q4), .clr(rst));
  Register #(.width(32)) x5 (.D(WD), .en(WE5), .clk(clk), .Q(Q5), .clr(rst));
  Register #(.width(32)) x6 (.D(WD), .en(WE6), .clk(clk), .Q(Q6), .clr(rst));
  Register #(.width(32)) x7 (.D(WD), .en(WE7), .clk(clk), .Q(Q7), .clr(rst));
  Register #(.width(32)) x8 (.D(WD), .en(WE8), .clk(clk), .Q(Q8), .clr(rst));
  Multiplexer #(.select(5), .width(32)) multiplexer_1 (
    .in0({32{1'b0}}), .in1(Q1), .in2(Q2), .in3(Q3), .in4(Q4), .in5(Q5), .in6(Q6), .in7(Q7), .in8(Q8),
    .in9(Q9), .in10(Q10), .in11(Q11), .in12(Q12), .in13(Q13), .in14(Q14), .in15(Q15), .in16(Q16), .in17(Q17),
    .in18(Q18), .in19(Q19), .in20(Q20), .in21(Q21), .in22(Q22), .in23(Q23), .in24(Q24), .in25(Q25),
    .in26(Q26), .in27(Q27), .in28(Q28), .in29(Q29), .in30(Q30), .in31(Q31), .out(RD1), .sel(RA1));
  Register #(.width(32)) x9 (.D(WD), .en(WE9), .clk(clk), .Q(Q9), .clr(rst));
  Register #(.width(32)) x10 (.D(WD), .en(WE10), .clk(clk), .Q(Q10), .clr(rst));
  Register #(.width(32)) x11 (.D(WD), .en(WE11), .clk(clk), .Q(Q11), .clr(rst));
  Register #(.width(32)) x12 (.D(WD), .en(WE12), .clk(clk), .Q(Q12), .clr(rst));
  Register #(.width(32)) x13 (.D(WD), .en(WE13), .clk(clk), .Q(Q13), .clr(rst));
  Register #(.width(32)) x14 (.D(WD), .en(WE14), .clk(clk), .Q(Q14), .clr(rst));
  Register #(.width(32)) x15 (.D(WD), .en(WE15), .clk(clk), .Q(Q15), .clr(rst));
  Register #(.width(32)) x16 (.D(WD), .en(WE16), .clk(clk), .Q(Q16), .clr(rst));
  Multiplexer #(.select(5), .width(32)) multiplexer_2 (
    .in0({32{1'b0}}), .in1(Q1), .in2(Q2), .in3(Q3), .in4(Q4), .in5(Q5), .in6(Q6), .in7(Q7), .in8(Q8),
    .in9(Q9), .in10(Q10), .in11(Q11), .in12(Q12), .in13(Q13), .in14(Q14), .in15(Q15), .in16(Q16), .in17(Q17),
    .in18(Q18), .in19(Q19), .in20(Q20), .in21(Q21), .in22(Q22), .in23(Q23), .in24(Q24), .in25(Q25),
    .in26(Q26), .in27(Q27), .in28(Q28), .in29(Q29), .in30(Q30), .in31(Q31), .out(RD2), .sel(RA2));
  // Probe on RA2
  Register #(.width(32)) x17 (.D(WD), .en(WE17), .clk(clk), .Q(Q17), .clr(rst));
  Register #(.width(32)) x18 (.D(WD), .en(WE18), .clk(clk), .Q(Q18), .clr(rst));
  Register #(.width(32)) x19 (.D(WD), .en(WE19), .clk(clk), .Q(Q19), .clr(rst));
  Register #(.width(32)) x20 (.D(WD), .en(WE20), .clk(clk), .Q(Q20), .clr(rst));
  Register #(.width(32)) x21 (.D(WD), .en(WE21), .clk(clk), .Q(Q21), .clr(rst));
  Register #(.width(32)) x22 (.D(WD), .en(WE22), .clk(clk), .Q(Q22), .clr(rst));
  Register #(.width(32)) x23 (.D(WD), .en(WE23), .clk(clk), .Q(Q23), .clr(rst));
  Register #(.width(32)) x24 (.D(WD), .en(WE24), .clk(clk), .Q(Q24), .clr(rst));
  Register #(.width(32)) x25 (.D(WD), .en(WE25), .clk(clk), .Q(Q25), .clr(rst));
  Register #(.width(32)) x26 (.D(WD), .en(WE26), .clk(clk), .Q(Q26), .clr(rst));
  Register #(.width(32)) x27 (.D(WD), .en(WE27), .clk(clk), .Q(Q27), .clr(rst));
  Register #(.width(32)) x28 (.D(WD), .en(WE28), .clk(clk), .Q(Q28), .clr(rst));
  Register #(.width(32)) x29 (.D(WD), .en(WE29), .clk(clk), .Q(Q29), .clr(rst));
  Register #(.width(32)) x30 (.D(WD), .en(WE30), .clk(clk), .Q(Q30), .clr(rst));
  Register #(.width(32)) x31 (.D(WD), .en(WE31), .clk(clk), .Q(Q31), .clr(rst));
endmodule

module ImmGen (
  input  [31:0] Inst,
  input  [2:0] ImmSrc,
  output [31:0] ImmExt
);

  wire [31:0] Imm_B, Imm_I, Imm_J, Imm_S;

  assign Imm_I = {{20{Inst[31]}}, Inst[31:20]};  // Bit_Extender bit_extender_1
  assign Imm_S = {{20{Inst[31]}}, {Inst[31:25], Inst[11:7]}};  // Bit_Extender bit_extender_2
  assign Imm_J = {{11{Inst[31]}}, {Inst[31], Inst[19:12], Inst[20], Inst[30:21], 1'b0}};  // Bit_Extender bit_extender_3
  assign Imm_B = {{19{Inst[31]}}, {Inst[31], Inst[7], Inst[30:25], Inst[11:8], 1'b0}};  // Bit_Extender bit_extender_4
  Multiplexer #(.select(3), .width(32)) multiplexer_1 (
    .in0(Imm_I), .in1({32{1'b0}}), .in2(Imm_S), .in3(Imm_B), .in4(Imm_J), .in5({Inst[31:12], {12{1'b0}}}),
    .out(ImmExt), .sel(ImmSrc));  // open: in6, in7

  // Other names for the same wires on the sheet: Imm_U[31:12] = Inst[31:12]
endmodule

module BranchUnit (
  input  [2:0] BranchOp,
  input  Zero,
  input  Less,
  output Branch
);

  wire not_1_out, not_2_out, not_3_out;

  not not_1 (not_1_out, Zero);
  not not_2 (not_2_out, Less);
  not not_3 (not_3_out, Less);
  Multiplexer #(.select(3)) multiplexer_1 (
    .in0(Zero), .in1(not_1_out), .in2(1'b0), .in3(1'b0), .in4(Less), .in5(not_2_out), .in6(Less),
    .in7(not_3_out), .out(Branch), .sel(BranchOp));
endmodule

module Control (
  input  [31:0] Inst,
  output RegWrite,
  output [1:0] ResultSrc,
  output MemWrite,
  output [2:0] MemOp,
  output [3:0] AluOp,
  output AluSrcA,
  output AluSrcB,
  output PcAddSrcA,
  output Branch,
  output Jump,
  output [2:0] BranchOp,
  output [2:0] ImmSrc
);

  wire and_1_out, and_2_out, Funct3000, Funct3010, Funct3111, is_Iarith, is_jal, is_lui, is_R,
       is_Roris_Iarith, is_sub;
  wire [3:0] multiplexer_1_out, multiplexer_2_out, multiplexer_3_out, multiplexer_4_out;

  Multiplexer #(.width(4)) multiplexer_1 (.in0(4'b0000), .in1(4'b1010), .out(multiplexer_1_out), .sel(is_lui));
  Comparator #(.width(7)) comparator_1 (.a(Inst[6:0]), .b(7'b0110011), .eq(is_R));  // open: gt, lt
  Comparator #(.width(7)) comparator_2 (.a(Inst[6:0]), .b(7'b0010011), .eq(is_Iarith));  // open: gt, lt
  Comparator #(.width(7)) comparator_3 (.a(Inst[6:0]), .b(7'b0000011), .eq(ResultSrc[0]));  // open: gt, lt
  Comparator #(.width(7)) comparator_4 (.a(Inst[6:0]), .b(7'b0100011), .eq(MemWrite));  // open: gt, lt
  or or_1 (ImmSrc[0], Branch, is_lui, AluSrcA);
  or or_2 (ImmSrc[1], MemWrite, Branch);
  or or_3 (ImmSrc[2], is_jal, is_lui, AluSrcA);
  Multiplexer #(.width(4)) multiplexer_2 (
    .in0(multiplexer_1_out), .in1(4'b0001), .out(multiplexer_2_out), .sel(Branch));
  or or_4 (RegWrite, is_R, is_Iarith, ResultSrc[0], is_jal, PcAddSrcA, is_lui, AluSrcA);
  Multiplexer #(.width(4)) multiplexer_3 (
    .in0(multiplexer_2_out), .in1(4'b0001), .out(multiplexer_3_out), .sel(is_sub));
  and and_1 (and_1_out, Funct3010, is_Roris_Iarith);
  Multiplexer #(.width(4)) multiplexer_4 (
    .in0(multiplexer_3_out), .in1(4'b0101), .out(multiplexer_4_out), .sel(and_1_out));
  and and_2 (and_2_out, is_Roris_Iarith, Funct3111);
  Comparator #(.width(3)) comparator_5 (.a(Inst[14:12]), .b(3'b010), .eq(Funct3010));  // open: gt, lt
  Comparator #(.width(3)) comparator_6 (.a(Inst[14:12]), .b(3'b000), .eq(Funct3000));  // open: gt, lt
  Comparator #(.width(3)) comparator_7 (.a(Inst[14:12]), .b(3'b111), .eq(Funct3111));  // open: gt, lt
  Comparator #(.width(7)) comparator_8 (.a(Inst[6:0]), .b(7'b1100011), .eq(Branch));  // open: gt, lt
  Comparator #(.width(7)) comparator_9 (.a(Inst[6:0]), .b(7'b1101111), .eq(is_jal));  // open: gt, lt
  Comparator #(.width(7)) comparator_10 (.a(Inst[6:0]), .b(7'b1100111), .eq(PcAddSrcA));  // open: gt, lt
  Comparator #(.width(7)) comparator_11 (.a(Inst[6:0]), .b(7'b0110111), .eq(is_lui));  // open: gt, lt
  Comparator #(.width(7)) comparator_12 (.a(Inst[6:0]), .b(7'b0010111), .eq(AluSrcA));  // open: gt, lt
  and and_3 (is_sub, is_R, Funct3000, Inst[30]);
  Multiplexer #(.width(4)) multiplexer_5 (.in0(multiplexer_4_out), .in1(4'b0010), .out(AluOp), .sel(and_2_out));
  or or_5 (Jump, is_jal, PcAddSrcA);
  or or_6 (AluSrcB, is_lui, AluSrcA, is_Iarith, ResultSrc[0], MemWrite, PcAddSrcA);
  or or_7 (is_Roris_Iarith, is_R, is_Iarith);

  assign BranchOp = Inst[14:12];
  assign MemOp = Inst[14:12];
  assign ResultSrc[1] = Jump;

  // Other names for the same wires on the sheet: Opcode[6:0] = Inst[6:0]; Funct3[2:0] = Inst[14:12];
  //   Funct7_5 = Inst[30]; is_auipc = AluSrcA; is_branch = Branch; is_jalr = PcAddSrcA; is_store = MemWrite;
  //   is_load = ResultSrc[0]
endmodule

module LSU (
  input  [31:0] Rs2,
  input  [1:0] Addr2,
  input  [2:0] MemOp,
  input  MemWrite,
  input  [31:0] MemReadData,
  output [31:0] MemWriteData,
  output [3:0] MemByteEnable,
  output [31:0] LoadResult
);

  wire is_byte_op, undriven;
  wire [3:0] Mask_Byte, Mask_Raw, MemWrite_4bit;
  wire [7:0] Selected_Byte;
  wire [31:0] lb_Result, Rs2_next, Rs2_shifted;

  Decoder #(.select(2)) decoder_1 (
    .out0(Mask_Byte[0]), .out1(Mask_Byte[1]), .out2(Mask_Byte[2]), .out3(Mask_Byte[3]), .sel(Addr2));  // open: en
  // Probe on undriven
  assign Rs2_next = {{24{1'b0}}, Rs2[7:0]};  // Bit_Extender bit_extender_1
  not not_1 (is_byte_op, MemOp[1]);
  Multiplexer #(.width(4)) multiplexer_1 (.in0(4'b1111), .in1(Mask_Byte), .out(Mask_Raw), .sel(is_byte_op));
  assign MemWrite_4bit = {{3{MemWrite}}, MemWrite};  // Bit_Extender bit_extender_2
  assign MemByteEnable = MemWrite_4bit & Mask_Raw;  // AND_Gate and_1, 4 bits wide
  Shifter #(.width(32)) shifter_1 (.in(Rs2_next), .\dist ({Addr2, 3'b000}), .out(Rs2_shifted));
  Multiplexer #(.width(32)) multiplexer_2 (.in0(Rs2), .in1(Rs2_shifted), .out(MemWriteData), .sel(is_byte_op));
  Multiplexer #(.select(2), .width(8)) multiplexer_3 (
    .in0(MemReadData[7:0]), .in1(MemReadData[15:8]), .in2(MemReadData[23:16]), .in3(MemReadData[31:24]),
    .out(Selected_Byte), .sel(Addr2));
  assign lb_Result = {{24{Selected_Byte[7]}}, Selected_Byte};  // Bit_Extender bit_extender_3
  Multiplexer #(.width(32)) multiplexer_4 (.in0(MemReadData), .in1(lb_Result), .out(LoadResult), .sel(is_byte_op));
  // Probe on nothing

  // Other names for the same wires on the sheet: Addr2_shifted[4:3] = Addr2; Byte0[7:0] = MemReadData[7:0];
  //   Byte1[7:0] = MemReadData[15:8]; Byte2[7:0] = MemReadData[23:16]; Byte3[7:0] = MemReadData[31:24];
  //   Rs2_lo8[7:0] = Rs2[7:0]
endmodule
